# Fritzing sketch fsr (saved by Fritzing 0.9.9b)
breadboards: 1

parts:
  R1 = Resistor [tolerance=±5% power=0.25 resistance=220 package=THT]
  LED1 = LED - 5mm [color="Red (633nm)" current=0.030 package="5 mm [THT]"]
  J1 = Basic Force Sensing Resistor (FSR) [package=THT]
  R2 = Resistor [tolerance=±5% power=0.25 resistance=10k package=THT]
  Part1 = Arduino Uno (Rev3)

nets:
  N1: R1.Pin_0, R2.Pin_1, Part1.GND
  N2: R1.Pin_1, LED1.cathode
  N3: LED1.anode, Part1.D3_PWM
  N4: J1.pin_0, Part1.5V
  N5: J1.pin_1, R2.Pin_0, Part1.A0
