# Fritzing sketch thumbjoystick (saved by Fritzing 0.9.10b)
circuit board: 2.83847cm x 4.50913cm
breadboards: 1

parts:
  Cyberinet_Joystick_Expansion_V1 = Thumb Joystick
  VCC_V_H_B_GND = female pin header, 5 pins [form="♀ (female)"]
  R1_220 = Resistor [tolerance=±5% resistance=220 power=0.25 package="0603 [SMD]"]
  (+)red_LED = smd LED [color="Red (633nm)" package="0603 [SMD]"]

nets:
  N1: Cyberinet_Joystick_Expansion_V1.GND, VCC_V_H_B_GND.pin1, R1_220.Pin_1
  N2: Cyberinet_Joystick_Expansion_V1.SEL, VCC_V_H_B_GND.pin2
  N3: Cyberinet_Joystick_Expansion_V1.HORZ, VCC_V_H_B_GND.pin3
  N4: Cyberinet_Joystick_Expansion_V1.VERT, VCC_V_H_B_GND.pin4
  N5: Cyberinet_Joystick_Expansion_V1.VCC, VCC_V_H_B_GND.pin5, (+)red_LED.cathode
  N6: R1_220.Pin_0, (+)red_LED.anode
