# Fritzing sketch micBasic (saved by Fritzing 0.9.10b)
circuit board: 2.00559cm x 4.58022cm
breadboards: 1

parts:
  A_GND_VCC_D = female pin header, 4 pins [form="♀ (female)"]
  J2 = female pin header, 4 pins [form="♀ (female)"]
  R1_(220) = Resistor [tolerance=±5% resistance=220 power=0.25 package="0603 [SMD]"]  # not connected
  LED1_(+) = smd LED [color="Red (633nm)" package="0603 [SMD]"]  # not connected

nets:
  N1: A_GND_VCC_D.pin1, J2.pin1
  N2: A_GND_VCC_D.pin2, J2.pin2
  N3: A_GND_VCC_D.pin3, J2.pin3
  N4: A_GND_VCC_D.pin4, J2.pin4
